# Fritzing sketch BeerController (saved by Fritzing 1.0.7)
stripboards: 1

parts:
  Q1 = NPN-Transistor [package="TO92 [THT]"]
  Q2 = NPN-Transistor [package="TO92 [THT]"]
  J2 = Camdenboss CTB0158-2 [part_number=CTB0158-2 package=THT]
  R1 = Resistor [tolerance=±5% power=0.25W resistance=1k package=THT]
  R2 = Resistor [tolerance=±5% power=0.25W resistance=10k package=THT]
  R3 = Resistor [tolerance=±5% power=0.25W resistance=4.7k package=THT]
  Q3 = NPN-Transistor [package="TO92 [THT]"]
  J1 = female pin header, 2 pins [form="♀ (female)"]
  R4 = Resistor [tolerance=±5% power=0.25W resistance=1k package=THT]
  Q4 = NPN-Transistor [package="TO92 [THT]"]
  R5 = Resistor [tolerance=±5% power=0.25W resistance=1k package=THT]
  DS1 = female pin header, 3 pins [form="♀ (female)"]
  DS2 = female pin header, 3 pins [form="♀ (female)"]
  pt1 = female pin header, 8 pins [form="♀ (female)"]
  pt2 = female pin header, 8 pins [form="♀ (female)"]
  DS-SGN = female pin header, 2 pins [form="♀ (female)"]
  spi = female pin header, 8 pins [form="♀ (female)"]
  DS3 = DS18B20 1-Wire Temperature Sensor [part_number=DS18B20]
  R6 = Resistor [tolerance=±5% resistance=4.7k package="0603 [SMD]"]

nets:
  N1: Q1.E, Q2.C
  N2: Q1.B, R1.Pin_1
  N3: Q1.C, J2.pin2
  GND: Q2.E, Q3.E, Q4.E, DS1.pin1, DS2.pin1, pt1.pin1, pt2.pin1, spi.pin1, DS3.GND
  N4: Q2.B, R2.Pin_1
  N5: J2.pin1, Q4.C
  N6: R1.Pin_0, J1.pin2
  N7: R2.Pin_0, R3.Pin_1, Q3.C
  3.3V: R3.Pin_0, DS1.pin2, DS2.pin2, pt1.pin2, pt2.pin2, spi.pin2, DS3.VDD, R6.Pin_0
  N8: Q3.B, R4.Pin_1
  N9: J1.pin1, R4.Pin_0, R5.Pin_0
  N10: Q4.B, R5.Pin_1
  N11: DS1.pin3, DS2.pin3, DS-SGN.pin2, DS3.DQ, R6.Pin_1
  N12: pt1.pin4, pt2.pin4, spi.pin4
  N13: pt1.pin5, pt2.pin5, spi.pin5
  N14: pt1.pin6, pt2.pin6, spi.pin6
  N15: pt1.pin7, spi.pin7
  N16: pt2.pin7, spi.pin8

notes:
  B
  A
  B-SSR
  A-SSR
  Vcc
  GND
